// Logisim project Clock.circ as structural Verilog: 6 circuits, main circuit clk
module clk (
);

  wire main_1_h0, main_1_h0_2, main_1_h1, main_1_h1_2, main_1_h2, main_1_h2_2, main_1_h3, main_1_h3_2,
       main_1_h4, main_1_h4_2, main_1_h5, main_1_h5_2, main_1_h6, main_1_h6_2, main_1_m0, main_1_m0_2,
       main_1_m1, main_1_m1_2, main_1_m2, main_1_m2_2, main_1_m3, main_1_m3_2, main_1_m4, main_1_m4_2,
       main_1_m5, main_1_m5_2, main_1_m6, main_1_m6_2, main_1_s0, main_1_s0_2, main_1_s1, main_1_s1_2,
       main_1_s2, main_1_s2_2, main_1_s3, main_1_s3_2, main_1_s4, main_1_s4_2, main_1_s5, main_1_s5_2,
       main_1_s6, main_1_s6_2;

  _7_Segment_Display u_7_segment_display_1 (
    .g(main_1_h0), .f(main_1_h1), .a(main_1_h2), .b(main_1_h3), .e(main_1_h4), .d(main_1_h5), .c(main_1_h6));  // open: dp
  main main_1 (
    .H2(main_1_h2), .h2_2(main_1_h2_2), .M2(main_1_m2), .m2_2(main_1_m2_2), .S2(main_1_s2),
    .s2_2(main_1_s2_2), .H3(main_1_h3), .h3_2(main_1_h3_2), .M3(main_1_m3), .m3_2(main_1_m3_2),
    .S3(main_1_s3), .s3_2(main_1_s3_2), .H6(main_1_h6), .h6_2(main_1_h6_2), .M6(main_1_m6),
    .m6_2(main_1_m6_2), .S6(main_1_s6), .s6_2(main_1_s6_2), .H5(main_1_h5), .h5_2(main_1_h5_2),
    .M5(main_1_m5), .m5_2(main_1_m5_2), .S5(main_1_s5), .s5_2(main_1_s5_2), .H4(main_1_h4),
    .h4_2(main_1_h4_2), .M4(main_1_m4), .m4_2(main_1_m4_2), .S4(main_1_s4), .s4_2(main_1_s4_2),
    .H1(main_1_h1), .h1_2(main_1_h1_2), .M1(main_1_m1), .m1_2(main_1_m1_2), .S1(main_1_s1),
    .s1_2(main_1_s1_2), .H0(main_1_h0), .h0_2(main_1_h0_2), .M0(main_1_m0), .m0_2(main_1_m0_2),
    .S0(main_1_s0), .s0_2(main_1_s0_2));
  _7_Segment_Display u_7_segment_display_2 (
    .g(main_1_h0_2), .f(main_1_h1_2), .a(main_1_h2_2), .b(main_1_h3_2), .e(main_1_h4_2), .d(main_1_h5_2),
    .c(main_1_h6_2));  // open: dp
  _7_Segment_Display u_7_segment_display_3 (
    .g(main_1_m0), .f(main_1_m1), .a(main_1_m2), .b(main_1_m3), .e(main_1_m4), .d(main_1_m5), .c(main_1_m6));  // open: dp
  _7_Segment_Display u_7_segment_display_4 (
    .g(main_1_m0_2), .f(main_1_m1_2), .a(main_1_m2_2), .b(main_1_m3_2), .e(main_1_m4_2), .d(main_1_m5_2),
    .c(main_1_m6_2));  // open: dp
  _7_Segment_Display u_7_segment_display_5 (
    .g(main_1_s0), .f(main_1_s1), .a(main_1_s2), .b(main_1_s3), .e(main_1_s4), .d(main_1_s5), .c(main_1_s6));  // open: dp
  _7_Segment_Display u_7_segment_display_6 (
    .g(main_1_s0_2), .f(main_1_s1_2), .a(main_1_s2_2), .b(main_1_s3_2), .e(main_1_s4_2), .d(main_1_s5_2),
    .c(main_1_s6_2));  // open: dp

  // Notes on the sheet:
  //   24 Hour Clock
endmodule

module main (
  output H2,
  output h2_2,
  output M2,
  output m2_2,
  output S2,
  output s2_2,
  output H3,
  output h3_2,
  output M3,
  output m3_2,
  output S3,
  output s3_2,
  output H6,
  output h6_2,
  output M6,
  output m6_2,
  output S6,
  output s6_2,
  output H5,
  output h5_2,
  output M5,
  output m5_2,
  output S5,
  output s5_2,
  output H4,
  output h4_2,
  output M4,
  output m4_2,
  output S4,
  output s4_2,
  output H1,
  output h1_2,
  output M1,
  output m1_2,
  output S1,
  output s1_2,
  output H0,
  output h0_2,
  output M0,
  output m0_2,
  output S0,
  output s0_2
);

  wire and_1_out, and_2_out, and_3_out, and_4_out, clock_1_out, counter_mod_2_1_a, counter_mod_2_1_b,
       counter_mod_2_1_is_bit_2, counter_mod_6_1_is_5, counter_mod_6_1_out_3, counter_mod_6_1_out_4,
       counter_mod_6_1_out_5, counter_mod_6_2_is_5, counter_mod_6_2_out_3, counter_mod_6_2_out_4,
       counter_mod_6_2_out_5, counter_mod_10_1_is_bit_4, counter_mod_10_1_is_bit_9, counter_mod_10_1_q0,
       counter_mod_10_1_q1, counter_mod_10_1_q2, counter_mod_10_1_q3, counter_mod_10_2_is_bit_9,
       counter_mod_10_2_q0, counter_mod_10_2_q1, counter_mod_10_2_q2, counter_mod_10_2_q3,
       counter_mod_10_3_is_bit_9, counter_mod_10_3_q0, counter_mod_10_3_q1, counter_mod_10_3_q2,
       counter_mod_10_3_q3;

  _7_segment_display u_7_segment_display_1 (
    .A(1'b0), .B(1'b0), .C(counter_mod_2_1_b), .D(counter_mod_2_1_a), .a_2(H2), .b_2(H3), .c_2(H6), .d_2(H5),
    .e(H4), .f(H1), .g(H0));  // open: h
  counter_mod_2 counter_mod_2_1 (
    .b(counter_mod_2_1_b), .a(counter_mod_2_1_a), .clk(clock_1_out), .IS_Bit_2(counter_mod_2_1_is_bit_2),
    .in_3(counter_mod_10_1_is_bit_4), .\input (and_1_out));
  and and_1 (and_1_out, counter_mod_10_1_is_bit_9, and_2_out);
  _7_segment_display u_7_segment_display_2 (
    .A(counter_mod_10_1_q0), .B(counter_mod_10_1_q1), .C(counter_mod_10_1_q2), .D(counter_mod_10_1_q3),
    .a_2(h2_2), .b_2(h3_2), .c_2(h6_2), .d_2(h5_2), .e(h4_2), .f(h1_2), .g(h0_2));  // open: h
  counter_mod_10 counter_mod_10_1 (
    .clk(clock_1_out), .Q3(counter_mod_10_1_q3), .Q2(counter_mod_10_1_q2), .Q1(counter_mod_10_1_q1),
    .Q0(counter_mod_10_1_q0), .IS_BIT_9(counter_mod_10_1_is_bit_9),
    .is_before_bit_2(counter_mod_2_1_is_bit_2), .is_Bit_4(counter_mod_10_1_is_bit_4), .\input (and_2_out));
  _7_segment_display u_7_segment_display_3 (
    .A(1'b0), .B(counter_mod_6_1_out_3), .C(counter_mod_6_1_out_5), .D(counter_mod_6_1_out_4), .a_2(M2),
    .b_2(M3), .c_2(M6), .d_2(M5), .e(M4), .f(M1), .g(M0));  // open: h
  and and_2 (and_2_out, counter_mod_6_1_is_5, and_3_out);
  counter_mod_6 counter_mod_6_1 (
    .out_4(counter_mod_6_1_out_4), .out_5(counter_mod_6_1_out_5), .out_3(counter_mod_6_1_out_3),
    .clk(clock_1_out), .IS_5(counter_mod_6_1_is_5), .in_1(and_3_out));
  and and_3 (and_3_out, counter_mod_10_2_is_bit_9, and_4_out);
  _7_segment_display u_7_segment_display_4 (
    .A(counter_mod_10_2_q0), .B(counter_mod_10_2_q1), .C(counter_mod_10_2_q2), .D(counter_mod_10_2_q3),
    .a_2(m2_2), .b_2(m3_2), .c_2(m6_2), .d_2(m5_2), .e(m4_2), .f(m1_2), .g(m0_2));  // open: h
  _7_segment_display u_7_segment_display_5 (
    .A(1'b0), .B(counter_mod_6_2_out_3), .C(counter_mod_6_2_out_5), .D(counter_mod_6_2_out_4), .a_2(S2),
    .b_2(S3), .c_2(S6), .d_2(S5), .e(S4), .f(S1), .g(S0));  // open: h
  counter_mod_10 counter_mod_10_2 (
    .clk(clock_1_out), .Q3(counter_mod_10_2_q3), .Q2(counter_mod_10_2_q2), .Q1(counter_mod_10_2_q1),
    .Q0(counter_mod_10_2_q0), .IS_BIT_9(counter_mod_10_2_is_bit_9), .\input (and_4_out));  // open: is_before_bit_2, is_Bit_4
  and and_4 (and_4_out, counter_mod_6_2_is_5, counter_mod_10_3_is_bit_9);
  counter_mod_6 counter_mod_6_2 (
    .out_4(counter_mod_6_2_out_4), .out_5(counter_mod_6_2_out_5), .out_3(counter_mod_6_2_out_3),
    .clk(clock_1_out), .IS_5(counter_mod_6_2_is_5), .in_1(counter_mod_10_3_is_bit_9));
  _7_segment_display u_7_segment_display_6 (
    .A(counter_mod_10_3_q0), .B(counter_mod_10_3_q1), .C(counter_mod_10_3_q2), .D(counter_mod_10_3_q3),
    .a_2(s2_2), .b_2(s3_2), .c_2(s6_2), .d_2(s5_2), .e(s4_2), .f(s1_2), .g(s0_2));  // open: h
  counter_mod_10 counter_mod_10_3 (
    .clk(clock_1_out), .Q3(counter_mod_10_3_q3), .Q2(counter_mod_10_3_q2), .Q1(counter_mod_10_3_q1),
    .Q0(counter_mod_10_3_q0), .IS_BIT_9(counter_mod_10_3_is_bit_9), .\input (1'b1));  // open: is_before_bit_2, is_Bit_4
  Clock clock_1 (.out(clock_1_out));
endmodule

module _7_segment_display (
  input  A,
  input  B,
  input  C,
  input  D,
  output a_2,
  output b_2,
  output c_2,
  output d_2,
  output e,
  output f,
  output g,
  output h
);

  wire and_1_out, and_2_out, and_3_out, and_4_out, and_5_out, and_6_out, and_7_out, and_8_out, and_9_out,
       and_10_out, and_11_out, and_12_out, and_13_out, and_14_out, and_15_out, and_16_out, not_1_out,
       not_2_out, not_3_out, not_4_out, not_5_out, not_6_out, not_7_out, not_8_out, not_9_out, not_10_out,
       not_11_out, not_12_out, not_13_out, not_14_out, not_15_out, not_16_out, not_17_out, not_18_out,
       not_19_out, not_20_out, not_21_out;

  not not_1 (not_1_out, B);
  and and_1 (and_1_out, not_1_out, not_2_out);
  not not_2 (not_2_out, D);
  and and_2 (and_2_out, B, D);
  not not_3 (not_3_out, B);
  not not_4 (not_4_out, C);
  and and_3 (and_3_out, not_4_out, not_5_out);
  not not_5 (not_5_out, D);
  and and_4 (and_4_out, C, D);
  not not_6 (not_6_out, C);
  or or_1 (c_2, not_6_out, D, B);
  not not_7 (not_7_out, B);
  and and_5 (and_5_out, not_7_out, not_8_out);
  not not_8 (not_8_out, D);
  not not_9 (not_9_out, B);
  and and_6 (and_6_out, not_9_out, C);
  and and_7 (and_7_out, C, not_10_out);
  not not_10 (not_10_out, D);
  and and_8 (and_8_out, B, not_11_out, D);
  not not_11 (not_11_out, C);
  not not_12 (not_12_out, B);
  and and_9 (and_9_out, not_12_out, not_13_out);
  not not_13 (not_13_out, D);
  and and_10 (and_10_out, C, not_14_out);
  not not_14 (not_14_out, D);
  not not_15 (not_15_out, C);
  and and_11 (and_11_out, not_15_out, not_16_out);
  not not_16 (not_16_out, D);
  and and_12 (and_12_out, B, not_17_out);
  not not_17 (not_17_out, C);
  and and_13 (and_13_out, B, not_18_out);
  not not_18 (not_18_out, D);
  not not_19 (not_19_out, B);
  and and_14 (and_14_out, not_19_out, C);
  and and_15 (and_15_out, B, not_20_out);
  not not_20 (not_20_out, C);
  and and_16 (and_16_out, B, not_21_out);
  not not_21 (not_21_out, D);
  or or_2 (a_2, and_1_out, C, and_2_out, A);
  or or_3 (b_2, not_3_out, and_3_out, and_4_out);
  or or_4 (d_2, and_5_out, and_6_out, and_7_out, and_8_out, A);
  or or_5 (e, and_9_out, and_10_out);
  or or_6 (f, and_11_out, and_12_out, and_13_out, A);
  or or_7 (g, and_14_out, and_15_out, and_16_out, A);

  assign h = 1'b0;
endmodule

module counter_mod_10 (
  input  \input ,
  input  is_before_bit_2,
  input  clk,
  output Q3,
  output Q2,
  output Q1,
  output Q0,
  output is_Bit_4,
  output IS_BIT_9
);

  wire and_1_out, and_2_out, and_3_out, and_5_out, and_6_out, and_7_out, or_1_out, t_ff_4_qn;

  T_Flip_Flop #(.trigger("falling")) t_ff_1 (
    .clk(and_1_out), .T(\input ), .Q(Q3), .reset(and_7_out));  // open: Qn, preset, en
  and and_1 (and_1_out, \input , clk);
  and and_2 (and_2_out, Q3, t_ff_4_qn);
  and and_3 (and_3_out, Q2, Q3);
  T_Flip_Flop #(.trigger("falling")) t_ff_2 (
    .clk(and_1_out), .T(and_2_out), .Q(Q2), .reset(and_7_out));  // open: Qn, preset, en
  and and_4 (IS_BIT_9, Q3, Q0);
  and and_5 (and_5_out, and_3_out, is_Bit_4);
  T_Flip_Flop #(.trigger("falling")) t_ff_3 (
    .clk(and_1_out), .T(and_3_out), .Q(is_Bit_4), .reset(and_7_out));  // open: Qn, preset, en
  or or_1 (or_1_out, and_5_out, and_6_out);
  and and_6 (and_6_out, Q0, Q3);
  T_Flip_Flop #(.trigger("falling")) t_ff_4 (
    .clk(and_1_out), .T(or_1_out), .Q(Q0), .Qn(t_ff_4_qn), .reset(and_7_out));  // open: preset, en
  and and_7 (and_7_out, is_before_bit_2, is_Bit_4);

  assign Q1 = is_Bit_4;
endmodule

module counter_mod_6 (
  input  in_1,
  input  clk,
  output out_3,
  output out_4,
  output out_5,
  output IS_5
);

  wire and_1_out, and_2_out, and_3_out, j_k_ff_3_qn;

  and and_1 (and_1_out, in_1, clk);
  J_K_Flip_Flop #(.trigger("falling")) j_k_ff_1 (
    .J(in_1), .clk(and_1_out), .K(in_1), .Q(out_4));  // open: Qn, preset, en, reset
  and and_2 (and_2_out, out_4, j_k_ff_3_qn);
  J_K_Flip_Flop #(.trigger("falling")) j_k_ff_2 (
    .J(and_2_out), .clk(and_1_out), .K(out_4), .Q(out_5));  // open: Qn, preset, en, reset
  and and_3 (and_3_out, out_5, out_4);
  J_K_Flip_Flop #(.trigger("falling")) j_k_ff_3 (
    .J(and_3_out), .clk(and_1_out), .K(out_4), .Q(out_3), .Qn(j_k_ff_3_qn));  // open: preset, en, reset
  and and_4 (IS_5, out_3, out_4);
endmodule

module counter_mod_2 (
  input  clk,
  input  \input ,
  input  in_3,
  output b,
  output a,
  output IS_Bit_2
);

  wire and_1_out, and_2_out, and_3_out, t_ff_2_qn, xor_1_out;

  and and_1 (and_1_out, clk, and_2_out);
  and and_2 (and_2_out, \input , t_ff_2_qn);
  T_Flip_Flop #(.trigger("falling")) t_ff_1 (
    .clk(and_1_out), .T(and_2_out), .Q(a), .reset(and_3_out));  // open: Qn, preset, en
  and and_3 (and_3_out, in_3, b);
  T_Flip_Flop #(.trigger("falling")) t_ff_2 (
    .clk(and_1_out), .T(xor_1_out), .Q(b), .Qn(t_ff_2_qn), .reset(and_3_out));  // open: preset, en
  xor xor_1 (xor_1_out, a, b);

  assign IS_Bit_2 = b;
endmodule
